# Fritzing sketch Untitled Sketch (saved by Fritzing 1.0.2b)

parts:
  Part1 = Arduino Uno (Rev3) - ICSP
  HC-SR04_Sensor_1 = HC-SR04 Ultrasonic Distance Sensor
  U1 = POT [knob_status=50% power=0.5W package=pot_mammoth]
  U2 = LCD-16X2 [package=lcd-16x2_noholes]

nets:
  N1: Part1.D8, HC-SR04_Sensor_1.ECHO
  N2: Part1.D9_PWM, HC-SR04_Sensor_1.TRIG
  N3: Part1.D11_PWM/MOSI, U2.E
  N4: Part1.D12/MISO, U2.RS
  N5: Part1.D2, U2.DB7
  N6: Part1.D3_PWM, U2.DB6
  N7: Part1.D4, U2.DB5
  N8: Part1.D5_PWM, U2.DB4
  5V: Part1.5V, U2.VDD
  N9: Part1.GND, U1.E
  N10: U1.A, U2.VO
